# Fritzing sketch Untitled Sketch (saved by Fritzing 0.9.3b)
circuit board: 8.46667cm x 5.64444cm
breadboards: 1

parts:
  U1 = ESP32-38PinWide [part_number=ESP32-38PinWide]
  LED1 = smd LED [color="Red (633nm)" package="0603 [SMD]"]
  LED2 = smd LED [color="Blue (525nm)" package="0603 [SMD]"]

nets:
  N1: U1.GPIO25, LED2.anode
  N2: U1.GPIO26, LED1.anode
  N3: U1.GND, LED1.cathode, LED2.cathode

custom parts:
  ESP32-38PinWide: Generic 38-Pin ESP32 with wide format (only access to one side of pins on a breadboard) based on Stephen Lilley's HiLetgo ESP-WROOM-32 ESP32 ESP-32S Development Board.

// code stored in the sketch: Untitled.ino

#include <WiFi.h>

const char* ssid = "home wifi name";
const char* password = "home wifi password";

WiFiServer server(80);

String header;



String output26State = "off";
String output27State = "off";

const int output26 = 26;
const int output27 = 27;


unsigned long currentTime = millis();

unsigned long previousTime = 0; 

const long timeoutTime = 2000;

void setup() {
  Serial.begin(115200);
 
  
  pinMode(output26, OUTPUT);
  pinMode(output27, OUTPUT);
  
 
  digitalWrite(output26, LOW);
  digitalWrite(output27, LOW);

 
  Serial.print("Connecting to ");
  Serial.println(ssid);
  WiFi.begin(ssid, password);
  while (WiFi.status() != WL_CONNECTED) {
    delay(500);
    Serial.print(".");
  }
  
  Serial.println("");
  Serial.println("WiFi connected.");
  Serial.println("IP address: ");
  Serial.println(WiFi.localIP());
  server.begin();
}

void loop(){
  WiFiClient client = server.available();  
  if (client) {                             
    currentTime = millis();
    previousTime = currentTime;
    Serial.println("New Client.");          
    String currentLine = "";               
    while (client.connected() && currentTime - previousTime <= timeoutTime) {  
      currentTime = millis();
      if (client.available()) {             
        char c = client.read();             
        Serial.write(c);                    
        header += c;
        if (c == '\n') {                    

          if (currentLine.length() == 0) {
            
            client.println("HTTP/1.1 200 OK");
            client.println("Content-type:text/html");
            client.println("Connection: close");
            client.println();
            
           
            if (header.indexOf("GET /26/on") >= 0) {
              Serial.println("GPIO 26 on");
              output26State = "on";
              digitalWrite(output26, HIGH);
            } else if (header.indexOf("GET /26/off") >= 0) {
              Serial.println("GPIO 26 off");
              output26State = "off";
              digitalWrite(output26, LOW);
            } else if (header.indexOf("GET /27/on") >= 0) {
              Serial.println("GPIO 27 on");
              output27State = "on";
              digitalWrite(output27, HIGH);
            } else if (header.indexOf("GET /27/off") >= 0) {
              Serial.println("GPIO 27 off");
              output27State = "off";
              digitalWrite(output27, LOW);
            } 
            
           
            client.println("<!DOCTYPE html><html>");
            client.println("<head><meta name=\"viewport\" content=\"width=device-width, initial-scale=1\">");
            client.println("<link rel=\"icon\" href=\"data:,\">");
            
            client.println("<style>html { font-family: Helvetica; display: inline-block; margin: 0px auto; text-align: center;}");
            client.println(".button { background-color: #4CAF50; border: none; color: white; padding: 16px 40px;");
            client.println("text-decoration: none; font-size: 30px; margin: 2px; cursor: pointer;}");
            client.println(".button2 {background-color: #555555;}</style></head>");
            
    
            client.println("<body><h1>ESP32 humoud Web Server/h1>");
            
           
            client.println("<p>GPIO 26 - State " + output26State + "</p>");
                   
            if (output26State=="off") {
              client.println("<p><a href=\"/26/on\"><button class=\"button\">ON</button></a></p>");
            } else {
              client.println("<p><a href=\"/26/off\"><button class=\"button button2\">OFF</button></a></p>");
            } 
               
              
            client.println("<p>GPIO 27 - State " + output27State + "</p>");
                  
            if (output27State=="off") {
              client.println("<p><a href=\"/27/on\"><button class=\"button\">ON</button></a></p>");
            } else {
              client.println("<p><a href=\"/27/off\"><button class=\"button button2\">OFF</button></a></p>");
            }
            client.println("</body></html>");

              
               
           
            client.println();
            
            break;
          } else { 
            currentLine = "";
          }
        } else if (c != '\r') {  
          currentLine += c;      
        }
      }
    }
    
    header = "";
   
    client.stop();
    Serial.println("Client disconnected.");
    Serial.println("");
  }
}
